// Logisim project VERSION FINAL.circ as structural Verilog: 12 circuits, main circuit main
module main (
);

  wire _0_out, _1_out, _2_out, _3_out, _4_out, _5_out, _6_out, _7_out, _8_out, _9_out, AC_out,
       alu_1_error_flag, alu_1_fact_f, alu_1_pow_flag, and_1_out, and_2_out, bcd_to_hex_1_changed,
       bcd_to_hex_1_negate, button_2_out, button_3_out, button_4_out, button_5_out, button_out, C_out,
       decoder_1_out1, decoder_1_out2, decoder_1_out3, decoder_1_out4, decoder_1_out5, decoder_1_out6,
       decoder_1_out7, decoder_1_out8, decoder_1_out9, decoder_1_out10, decoder_1_out11, decoder_1_out12,
       decoder_1_out13, decoder_1_out14, decoder_1_out15, DIV_out, E_out, ENT_out, Error_e_symbol, f_out,
       FAC_out, Flag_F_out, Flag_P_out, hex_to_bcd_1_sign, interrupt_1_effective_release_trigerred,
       interrupt_1_skip_interrupt_instructions, interrupt_2_skip_interrupt_instructions,
       interrupt_3_skip_interrupt_instructions, interrupt_4_skip_interrupt_instructions,
       interrupt_5_skip_interrupt_instructions, interrupt_6_skip_interrupt_instructions,
       interrupt_7_skip_interrupt_instructions, interrupt_8_skip_interrupt_instructions, MUL_out, n_out,
       not_1_out, NUM_out, OFF_out, ON_out, or_1_out, or_2_out, or_3_out, OUT_out, POW_out, Shift, SUB_out,
       SUM_out, wire_system_1_clock_line, wire_system_1_reset_calc;
  wire [3:0] hex_to_bcd_1_out_8, hex_to_bcd_1_out_9, hex_to_bcd_1_out_10, hex_to_bcd_1_out_11,
       hex_to_bcd_1_out_12;
  wire [7:0] counter_1_q;
  wire [11:0] rom_1_data;
  wire [15:0] alu_1_div, alu_1_div_remainer, alu_1_fact, alu_1_mul, alu_1_pow, alu_1_sub, alu_1_sum,
       bcd_to_hex_1_output, hex_to_bcd_1_buffer, multiplexer_1_out, register_1_q, register_2_q, S1, S2, S3,
       S4, S5, S6;

  Wire_System wire_system_1 (
    .On(ON_out), .Off(OFF_out), .Reset_Calc(wire_system_1_reset_calc), .Clock_Line(wire_system_1_clock_line));
  Button ON (.out(ON_out));
  Button OFF (.out(OFF_out));
  _7_Segment_Display u_7_segment_display_1 (.g(hex_to_bcd_1_sign));  // open: f, a, b, e, d, c, dp
  Button f (.out(f_out));
  Button button (.out(button_out));
  Button button_2 (.out(button_2_out));
  Button button_3 (.out(button_3_out));
  Hex_Digit_Display hex_digit_display_1 (.value(hex_to_bcd_1_out_8));  // open: dp
  Hex_Digit_Display hex_digit_display_2 (.value(hex_to_bcd_1_out_9));  // open: dp
  Button AC (.out(AC_out));
  Button C (.out(C_out));
  Button n (.out(n_out));
  Button button_4 (.out(button_4_out));
  Button _1 (.out(_1_out));
  Button button_5 (.out(button_5_out));
  Button _4 (.out(_4_out));
  Button _7 (.out(_7_out));
  Hex_to_BCD hex_to_bcd_1 (
    .Hex(multiplexer_1_out), .Load(decoder_1_out1), .Clock(wire_system_1_clock_line),
    .out_8(hex_to_bcd_1_out_8), .out_9(hex_to_bcd_1_out_9), .out_10(hex_to_bcd_1_out_10),
    .out_11(hex_to_bcd_1_out_11), .out_12(hex_to_bcd_1_out_12), .Sign(hex_to_bcd_1_sign),
    .Buffer(hex_to_bcd_1_buffer), .AC(AC_out), .C(C_out));
  Hex_Digit_Display hex_digit_display_3 (.value(hex_to_bcd_1_out_11));  // open: dp
  Hex_Digit_Display hex_digit_display_4 (.value(hex_to_bcd_1_out_10));  // open: dp
  Button E (.out(E_out));
  Button _0 (.out(_0_out));
  Button _2 (.out(_2_out));
  Button _3 (.out(_3_out));
  Button _6 (.out(_6_out));
  Button _5 (.out(_5_out));
  Button _8 (.out(_8_out));
  Button _9 (.out(_9_out));
  or or_1 (or_1_out, C_out, AC_out);
  _7_Segment_Display u_7_segment_display_2 (
    .g(Error_e_symbol), .f(Error_e_symbol), .a(Error_e_symbol), .e(Error_e_symbol), .d(Error_e_symbol));  // open: b, c, dp
  Hex_Digit_Display hex_digit_display_5 (.value(hex_to_bcd_1_out_12));  // open: dp
  LED NEGATIVE (.in(bcd_to_hex_1_negate));
  BCD_to_HEX bcd_to_hex_1 (
    .n(n_out), ._0(_0_out), .in_4(_1_out), .in_5(_2_out), .in_7(_4_out), .in_8(_5_out), .in_9(_6_out),
    .in_10(_7_out), .in_11(_8_out), .in_12(_9_out), .C(C_out), .Output(bcd_to_hex_1_output), .in_6(_3_out),
    .Changed(bcd_to_hex_1_changed), .Negate(bcd_to_hex_1_negate), .Change_Applied(OUT_out), .AC(AC_out),
    .BCD_Lowest(hex_to_bcd_1_out_12), .BCD_3(hex_to_bcd_1_out_11), .BCD_2(hex_to_bcd_1_out_10),
    .BCD(hex_to_bcd_1_out_9), .BCD_Biggest(hex_to_bcd_1_out_8), .Sync(Shift),
    .Clock_Line(wire_system_1_clock_line));
  Error_System Error (.Clear(or_1_out), .E_symbol(Error_e_symbol), .Error(alu_1_error_flag));
  and OUT (OUT_out, bcd_to_hex_1_changed, interrupt_1_effective_release_trigerred);
  Interrupt interrupt_1 (
    .Interrupt_Flag(bcd_to_hex_1_changed),
    .Skip_Interrupt_Instructions(interrupt_1_skip_interrupt_instructions),
    .Release_On_Instruction_Check(decoder_1_out3), .Clock_Line(wire_system_1_clock_line),
    .Effective_Release_Trigerred(interrupt_1_effective_release_trigerred));
  Interrupt interrupt_2 (
    .Interrupt_Flag(E_out), .Skip_Interrupt_Instructions(interrupt_2_skip_interrupt_instructions),
    .Release_On_Instruction_Check(decoder_1_out4), .Clock_Line(wire_system_1_clock_line));  // open: Effective_Release_Trigerred
  Interrupt interrupt_3 (
    .Interrupt_Flag(button_4_out), .Skip_Interrupt_Instructions(interrupt_3_skip_interrupt_instructions),
    .Release_On_Instruction_Check(decoder_1_out6), .Clock_Line(wire_system_1_clock_line));  // open: Effective_Release_Trigerred
  Interrupt interrupt_4 (
    .Interrupt_Flag(button_5_out), .Skip_Interrupt_Instructions(interrupt_4_skip_interrupt_instructions),
    .Release_On_Instruction_Check(decoder_1_out7), .Clock_Line(wire_system_1_clock_line));  // open: Effective_Release_Trigerred
  Interrupt interrupt_5 (
    .Interrupt_Flag(button_2_out), .Skip_Interrupt_Instructions(interrupt_5_skip_interrupt_instructions),
    .Release_On_Instruction_Check(decoder_1_out8), .Clock_Line(wire_system_1_clock_line));  // open: Effective_Release_Trigerred
  Interrupt interrupt_6 (
    .Interrupt_Flag(button_3_out), .Skip_Interrupt_Instructions(interrupt_6_skip_interrupt_instructions),
    .Release_On_Instruction_Check(decoder_1_out9), .Clock_Line(wire_system_1_clock_line));  // open: Effective_Release_Trigerred
  Interrupt interrupt_7 (
    .Interrupt_Flag(f_out), .Skip_Interrupt_Instructions(interrupt_7_skip_interrupt_instructions),
    .Release_On_Instruction_Check(decoder_1_out10), .Clock_Line(wire_system_1_clock_line));  // open: Effective_Release_Trigerred
  Interrupt interrupt_8 (
    .Interrupt_Flag(button_out), .Skip_Interrupt_Instructions(interrupt_8_skip_interrupt_instructions),
    .Release_On_Instruction_Check(decoder_1_out11), .Clock_Line(wire_system_1_clock_line));  // open: Effective_Release_Trigerred
  Smart_Stack smart_stack_1 (
    .Data_from_Enter(bcd_to_hex_1_output), .Data_from_ALU(hex_to_bcd_1_buffer), .AC(AC_out),
    .When_1__load_from_ALU(rom_1_data[0]), .Remainer_from_ALU(alu_1_div_remainer),
    .Prepare_Rem(decoder_1_out15), .Put_Rem(rom_1_data[4]), .Shift(Shift), .S1(S1), .S2(S2), .S3(S3),
    .S4(S4), .S5(S5), .S6(S6), .No_push_insert(and_2_out), .Extra_Data(alu_1_fact), .No_push_mux(and_1_out));
  and ENT (ENT_out, interrupt_2_skip_interrupt_instructions, decoder_1_out4);
  and NUM (NUM_out, interrupt_1_skip_interrupt_instructions, decoder_1_out3);
  or or_2 (or_2_out, decoder_1_out2, NUM_out, ENT_out, SUM_out, SUB_out, MUL_out, DIV_out, FAC_out, POW_out);
  Counter counter_1 (
    .load(or_2_out), .D(rom_1_data[7:0]), .count(not_1_out), .Q(counter_1_q), .clk(wire_system_1_clock_line),
    .clr(wire_system_1_reset_calc));  // open: carry, preset, down
  and SUB (SUB_out, interrupt_4_skip_interrupt_instructions, decoder_1_out7);
  and SUM (SUM_out, interrupt_3_skip_interrupt_instructions, decoder_1_out6);
  and MUL (MUL_out, interrupt_5_skip_interrupt_instructions, decoder_1_out8);
  and DIV (DIV_out, interrupt_6_skip_interrupt_instructions, decoder_1_out9);
  and POW (POW_out, interrupt_8_skip_interrupt_instructions, decoder_1_out11);
  and FAC (FAC_out, interrupt_7_skip_interrupt_instructions, decoder_1_out10);
  ROM #(.dataWidth(12), .Select("low")) rom_1 (.addr(counter_1_q), .data(rom_1_data));
  and Flag_F (Flag_F_out, decoder_1_out12, ~alu_1_fact_f, ~rom_1_data[4]);  // AND_Gate
  and Flag_P (Flag_P_out, decoder_1_out12, ~alu_1_pow_flag, rom_1_data[4]);  // AND_Gate
  or or_3 (or_3_out, Flag_F_out, Flag_P_out);
  not not_1 (not_1_out, or_3_out);
  and and_1 (and_1_out, decoder_1_out14, rom_1_data[4]);
  and and_2 (and_2_out, decoder_1_out14, rom_1_data[0]);
  and u_Shift (Shift, decoder_1_out13, rom_1_data[4]);
  ALU alu_1 (
    .Op_1(register_1_q), .Op_2(register_2_q), .SUM(alu_1_sum), .SUB(alu_1_sub), .MUL(alu_1_mul),
    .DIV(alu_1_div), .DIV_Remainer(alu_1_div_remainer), .FACT(alu_1_fact), .POW(alu_1_pow),
    .Error_Flag(alu_1_error_flag), .Instruction(rom_1_data), .Fact_F(alu_1_fact_f),
    .Clock(wire_system_1_clock_line), .Pow_Flag(alu_1_pow_flag), .ALU_Called(decoder_1_out5),
    .Prepare_MUX(rom_1_data[4]), .Start_Calc(rom_1_data[0]));  // open: out_15
  Decoder #(.select(4), .enable("false")) decoder_1 (
    .out1(decoder_1_out1), .out2(decoder_1_out2), .out3(decoder_1_out3), .out4(decoder_1_out4),
    .out5(decoder_1_out5), .out6(decoder_1_out6), .out7(decoder_1_out7), .out8(decoder_1_out8),
    .out9(decoder_1_out9), .out10(decoder_1_out10), .out11(decoder_1_out11), .out12(decoder_1_out12),
    .out13(decoder_1_out13), .out14(decoder_1_out14), .out15(decoder_1_out15), .sel(rom_1_data[11:8]));  // open: out0
  Multiplexer #(.select(3), .width(16), .enable("false")) multiplexer_1 (
    .in0(bcd_to_hex_1_output), .in1(alu_1_sum), .in2(alu_1_sub), .in3(alu_1_mul), .in4(alu_1_div),
    .in5(alu_1_fact), .in6(alu_1_pow), .out(multiplexer_1_out), .sel(rom_1_data[2:0]));  // open: in7
  Register #(.width(16), .Select("low")) register_1 (
    .D(S1), .Q(register_1_q), .clk(wire_system_1_clock_line), .clr(AC_out));  // open: en
  Register #(.width(16), .Select("low")) register_2 (
    .D(S2), .Q(register_2_q), .clk(wire_system_1_clock_line), .clr(AC_out));  // open: en
  Register #(.width(16), .Select("low")) register_3 (
    .D(S3), .clk(wire_system_1_clock_line), .clr(AC_out));  // open: en, Q
  Register #(.width(16), .Select("low")) register_4 (
    .D(S4), .clk(wire_system_1_clock_line), .clr(AC_out));  // open: en, Q
  Register #(.width(16), .Select("low")) register_5 (
    .D(S5), .clk(wire_system_1_clock_line), .clr(AC_out));  // open: en, Q
  Register #(.width(16), .Select("low")) register_6 (
    .D(S6), .clk(wire_system_1_clock_line), .clr(AC_out));  // open: en, Q

  // Notes on the sheet:
  //   Calculator
  //   Range: -32768 a 32767
  //   contents of rom_1 (hex, n*v repeats v):
  //   0 303 100 607 101 d01 d11 70b 102 d01 d11 80f 103 d01 d11 915 104 f00 f10 d01 d11 a1e 500 510 511
  //   501 c00 105 e10 e11 b27 500 510 511 501 c11 106 d01 d11 42a d00 d10 201
  //   4 bits
  //   SP
  //   FP
  //   Remainer
  //   Exp
  //   Base
endmodule

// Output
module Hex_to_BCD (
  input  Clock,
  input  [15:0] Hex,
  input  Load,
  input  AC,
  input  C,
  output [15:0] Buffer,
  output Sign,
  output [3:0] out_8,
  output [3:0] out_9,
  output [3:0] out_10,
  output [3:0] out_11,
  output [3:0] out_12
);

  wire and_1_out, comparator_1_eq, comparator_2_eq, comparator_2_lt, hex_to_bcd_algorithm_2_carry_out,
       hex_to_bcd_algorithm_3_carry_out, hex_to_bcd_algorithm_4_carry_out, hex_to_bcd_algorithm_5_carry_out,
       hex_to_bcd_algorithm_6_carry_out, hex_to_bcd_algorithm_7_carry_out, hex_to_bcd_algorithm_8_carry_out,
       hex_to_bcd_algorithm_9_carry_out, or_1_out, or_2_out, two_complement_1_complement;
  wire [3:0] hex_to_bcd_algorithm_1_output, hex_to_bcd_algorithm_2_output, hex_to_bcd_algorithm_3_output,
       hex_to_bcd_algorithm_4_output, hex_to_bcd_algorithm_5_output, hex_to_bcd_algorithm_6_output,
       hex_to_bcd_algorithm_7_output, hex_to_bcd_algorithm_8_output, hex_to_bcd_algorithm_9_output,
       multiplexer_1_out, multiplexer_2_out, multiplexer_3_out, multiplexer_4_out, register_7_q,
       register_8_q, register_9_q, register_10_q, two_complement_1_out_1, two_complement_1_out_2,
       two_complement_1_out_3, two_complement_1_out_4;
  wire [4:0] counter_1_q;

  Counter #(.width(5), .max('h1f)) counter_1 (
    .count(comparator_2_lt), .Q(counter_1_q), .clk(Clock), .clr(or_1_out));  // open: load, D, carry, preset, down
  or or_1 (or_1_out, Load, AC, C);
  or or_2 (or_2_out, AC, C);
  Comparator #(.width(5), .mode("unsigned")) comparator_1 (
    .a(5'b00001), .b(counter_1_q), .eq(comparator_1_eq));  // open: gt, lt
  and and_1 (and_1_out, comparator_2_lt, Clock);
  Comparator #(.width(5), .mode("unsigned")) comparator_2 (
    .a(counter_1_q), .b(5'b10010), .eq(comparator_2_eq), .lt(comparator_2_lt));  // open: gt
  Register #(.width(16), .Select("low")) register_1 (.D(Hex), .Q(Buffer), .clk(or_1_out), .clr(or_2_out));  // open: en
  and and_2 (Sign, comparator_2_eq, two_complement_1_complement);
  Register #(.width(4), .Select("low")) register_2 (
    .D(hex_to_bcd_algorithm_1_output), .Q(out_8), .clk(and_1_out), .clr(or_1_out));  // open: en
  Hex_to_BCD_Algorithm hex_to_bcd_algorithm_1 (
    .Carry_In(hex_to_bcd_algorithm_2_carry_out), .Input(out_8), .Output(hex_to_bcd_algorithm_1_output),
    .Enable_Shift(comparator_2_lt));  // open: Carry_Out
  Hex_Digit_Display hex_digit_display_1 (.value(out_8));  // open: dp
  Register #(.width(4), .Select("low")) register_3 (
    .D(hex_to_bcd_algorithm_2_output), .Q(out_9), .clk(and_1_out), .clr(or_1_out));  // open: en
  Hex_to_BCD_Algorithm hex_to_bcd_algorithm_2 (
    .Carry_Out(hex_to_bcd_algorithm_2_carry_out), .Carry_In(hex_to_bcd_algorithm_3_carry_out), .Input(out_9),
    .Output(hex_to_bcd_algorithm_2_output), .Enable_Shift(comparator_2_lt));
  Hex_Digit_Display hex_digit_display_2 (.value(out_9));  // open: dp
  Two_Complement two_complement_1 (
    .Input_1(Buffer[15:12]), .Input_2(Buffer[11:8]), .Input_3(Buffer[7:4]), .Input_4(Buffer[3:0]),
    .Out_1(two_complement_1_out_1), .Out_2(two_complement_1_out_2), .Out_3(two_complement_1_out_3),
    .Out_4(two_complement_1_out_4), .Complement(two_complement_1_complement));
  Register #(.width(4), .Select("low")) register_4 (
    .D(hex_to_bcd_algorithm_3_output), .Q(out_10), .clk(and_1_out), .clr(or_1_out));  // open: en
  Hex_to_BCD_Algorithm hex_to_bcd_algorithm_3 (
    .Carry_Out(hex_to_bcd_algorithm_3_carry_out), .Carry_In(hex_to_bcd_algorithm_4_carry_out),
    .Input(out_10), .Output(hex_to_bcd_algorithm_3_output), .Enable_Shift(comparator_2_lt));
  Hex_Digit_Display hex_digit_display_3 (.value(out_10));  // open: dp
  Register #(.width(4), .Select("low")) register_5 (
    .D(hex_to_bcd_algorithm_4_output), .Q(out_11), .clk(and_1_out), .clr(or_1_out));  // open: en
  Hex_to_BCD_Algorithm hex_to_bcd_algorithm_4 (
    .Carry_Out(hex_to_bcd_algorithm_4_carry_out), .Carry_In(hex_to_bcd_algorithm_5_carry_out),
    .Input(out_11), .Output(hex_to_bcd_algorithm_4_output), .Enable_Shift(comparator_2_lt));
  Hex_Digit_Display hex_digit_display_4 (.value(out_11));  // open: dp
  Register #(.width(4), .Select("low")) register_6 (
    .D(hex_to_bcd_algorithm_5_output), .Q(out_12), .clk(and_1_out), .clr(or_1_out));  // open: en
  Hex_to_BCD_Algorithm hex_to_bcd_algorithm_5 (
    .Carry_Out(hex_to_bcd_algorithm_5_carry_out), .Carry_In(hex_to_bcd_algorithm_6_carry_out),
    .Input(out_12), .Output(hex_to_bcd_algorithm_5_output), .Enable_Shift(comparator_2_lt));
  Hex_Digit_Display hex_digit_display_5 (.value(out_12));  // open: dp
  Multiplexer #(.width(4), .enable("false")) multiplexer_1 (
    .in0(hex_to_bcd_algorithm_6_output), .in1(two_complement_1_out_1), .out(multiplexer_1_out),
    .sel(comparator_1_eq));
  Register #(.width(4), .Select("low")) register_7 (
    .D(multiplexer_1_out), .Q(register_7_q), .clk(and_1_out), .clr(or_1_out));  // open: en
  Hex_to_BCD_Algorithm hex_to_bcd_algorithm_6 (
    .Carry_Out(hex_to_bcd_algorithm_6_carry_out), .Carry_In(hex_to_bcd_algorithm_7_carry_out),
    .Input(register_7_q), .Output(hex_to_bcd_algorithm_6_output), .Enable_Shift(1'b0));
  Multiplexer #(.width(4), .enable("false")) multiplexer_2 (
    .in0(hex_to_bcd_algorithm_7_output), .in1(two_complement_1_out_2), .out(multiplexer_2_out),
    .sel(comparator_1_eq));
  Register #(.width(4), .Select("low")) register_8 (
    .D(multiplexer_2_out), .Q(register_8_q), .clk(and_1_out), .clr(or_1_out));  // open: en
  Hex_to_BCD_Algorithm hex_to_bcd_algorithm_7 (
    .Carry_Out(hex_to_bcd_algorithm_7_carry_out), .Carry_In(hex_to_bcd_algorithm_8_carry_out),
    .Input(register_8_q), .Output(hex_to_bcd_algorithm_7_output), .Enable_Shift(1'b0));
  Multiplexer #(.width(4), .enable("false")) multiplexer_3 (
    .in0(hex_to_bcd_algorithm_8_output), .in1(two_complement_1_out_3), .out(multiplexer_3_out),
    .sel(comparator_1_eq));
  Register #(.width(4), .Select("low")) register_9 (
    .D(multiplexer_3_out), .Q(register_9_q), .clk(and_1_out), .clr(or_1_out));  // open: en
  Hex_to_BCD_Algorithm hex_to_bcd_algorithm_8 (
    .Carry_Out(hex_to_bcd_algorithm_8_carry_out), .Carry_In(hex_to_bcd_algorithm_9_carry_out),
    .Input(register_9_q), .Output(hex_to_bcd_algorithm_8_output), .Enable_Shift(1'b0));
  Multiplexer #(.width(4), .enable("false")) multiplexer_4 (
    .in0(hex_to_bcd_algorithm_9_output), .in1(two_complement_1_out_4), .out(multiplexer_4_out),
    .sel(comparator_1_eq));
  Register #(.width(4), .Select("low")) register_10 (
    .D(multiplexer_4_out), .Q(register_10_q), .clk(and_1_out), .clr(or_1_out));  // open: en
  Hex_to_BCD_Algorithm hex_to_bcd_algorithm_9 (
    .Carry_Out(hex_to_bcd_algorithm_9_carry_out), .Carry_In(1'b0), .Input(register_10_q),
    .Output(hex_to_bcd_algorithm_9_output), .Enable_Shift(1'b0));
endmodule

module Hex_to_BCD_Algorithm (
  input  [3:0] Input,
  input  Enable_Shift,
  input  Carry_In,
  output Carry_Out,
  output [3:0] Output
);

  wire and_1_out, comparator_1_gt;
  wire [0:0] shifter_1_out;
  wire [2:0] multiplexer_1_out;
  wire [3:0] adder_1_out;

  Multiplexer #(.width(4), .enable("false")) multiplexer_1 (
    .in0(Input), .in1(adder_1_out), .out({Carry_Out, multiplexer_1_out}), .sel(and_1_out));
  Comparator #(.width(4), .mode("unsigned")) comparator_1 (
    .a(Input), .b(4'b0100), .gt(comparator_1_gt));  // open: eq, lt
  and and_1 (and_1_out, comparator_1_gt, Enable_Shift);
  Adder #(.width(4)) adder_1 (.a(Input), .b(4'b0011), .out(adder_1_out));  // open: cin, cout
  Shifter #(.width(4)) shifter_1 (
    .in({Carry_Out, multiplexer_1_out}), .\dist (2'b01), .out({Output[3:1], shifter_1_out[0]}));

  assign Output[0] = Carry_In;
endmodule

// Wire
module Wire_System (
  input  On,
  input  Off,
  output Reset_Calc,
  output Clock_Line
);

  wire clock_1_out, register_1_q;

  Clock clock_1 (.out(clock_1_out));
  Register #(.width(1), .Select("low")) register_1 (.D(On), .Q(register_1_q), .clk(On), .clr(Off));  // open: en
  and and_1 (Clock_Line, register_1_q, clock_1_out);

  assign Reset_Calc = Off;
endmodule

module Two_Complement (
  input  [3:0] Input_1,
  input  [3:0] Input_2,
  input  [3:0] Input_3,
  input  [3:0] Input_4,
  output [3:0] Out_1,
  output [3:0] Out_2,
  output [3:0] Out_3,
  output [3:0] Out_4,
  output Complement
);

  wire adder_1_cout, adder_2_cout, adder_3_cout;
  wire [3:0] adder_1_out, adder_2_out, adder_3_out, adder_4_out, not_1_out, not_2_out, not_3_out, not_4_out;

  assign not_1_out = ~Input_4;  // NOT_Gate not_1, 4 bits wide
  assign not_2_out = ~Input_3;  // NOT_Gate not_2, 4 bits wide
  assign not_3_out = ~Input_2;  // NOT_Gate not_3, 4 bits wide
  assign not_4_out = ~Input_1;  // NOT_Gate not_4, 4 bits wide
  Adder #(.width(4)) adder_1 (.a(not_1_out), .b(4'b0001), .out(adder_1_out), .cout(adder_1_cout));  // open: cin
  Adder #(.width(4)) adder_2 (.a(not_2_out), .b(4'b0000), .out(adder_2_out), .cin(adder_1_cout), .cout(adder_2_cout));
  Adder #(.width(4)) adder_3 (.a(not_3_out), .b(4'b0000), .out(adder_3_out), .cin(adder_2_cout), .cout(adder_3_cout));
  Adder #(.width(4)) adder_4 (.a(not_4_out), .b(4'b0000), .out(adder_4_out), .cin(adder_3_cout));  // open: cout
  Multiplexer #(.width(4), .enable("false")) multiplexer_1 (
    .in0(Input_4), .in1(adder_1_out), .out(Out_4), .sel(Input_1[3]));
  Multiplexer #(.width(4), .enable("false")) multiplexer_2 (
    .in0(Input_3), .in1(adder_2_out), .out(Out_3), .sel(Input_1[3]));
  Multiplexer #(.width(4), .enable("false")) multiplexer_3 (
    .in0(Input_2), .in1(adder_3_out), .out(Out_2), .sel(Input_1[3]));
  Multiplexer #(.width(4), .enable("false")) multiplexer_4 (
    .in0(Input_1), .in1(adder_4_out), .out(Out_1), .sel(Input_1[3]));

  assign Complement = Input_1[3];
endmodule

// Input
module BCD_to_HEX (
  input  Change_Applied,
  input  n,
  input  _0,
  input  in_4,
  input  in_5,
  input  in_6,
  input  in_7,
  input  in_8,
  input  in_9,
  input  in_10,
  input  in_11,
  input  in_12,
  input  C,
  input  AC,
  input  [3:0] BCD_Biggest,
  input  [3:0] BCD,
  input  [3:0] BCD_2,
  input  [3:0] BCD_3,
  input  [3:0] BCD_Lowest,
  input  Sync,
  input  Clock_Line,
  output Negate,
  output Changed,
  output [15:0] Output
);

  wire and_1_out, d_ff_1_qn, or_1_out, or_2_out, or_3_out, or_4_out, priority_encoder_1_gs, register_7_q,
       wait_1_same_bit, Wait_2_q, xor_1_out;
  wire [3:0] priority_encoder_1_out;
  wire [15:0] adder_1_out, adder_2_out, adder_3_out, adder_4_out, bit_extender_1_out, bit_extender_2_out,
       bit_extender_3_out, bit_extender_4_out, bit_extender_5_out, multiplexer_1_out, multiplexer_2_out,
       multiplexer_3_out, multiplexer_4_out, multiplexer_5_out, multiplier_1_out, multiplier_2_out,
       multiplier_3_out, multiplier_4_out, negator_1_out, register_1_q, register_2_q, register_3_q,
       register_4_q, register_5_q;

  Multiplexer #(.width(16), .enable("false")) multiplexer_1 (
    .in0(register_2_q), .in1(bit_extender_1_out), .out(multiplexer_1_out), .sel(wait_1_same_bit));
  or or_1 (or_1_out, C, AC);
  assign bit_extender_1_out = {{12{1'b0}}, BCD_Biggest};  // Bit_Extender bit_extender_1
  assign bit_extender_2_out = {{12{1'b0}}, BCD};  // Bit_Extender bit_extender_2
  assign bit_extender_3_out = {{12{1'b0}}, BCD_2};  // Bit_Extender bit_extender_3
  assign bit_extender_4_out = {{12{1'b0}}, BCD_3};  // Bit_Extender bit_extender_4
  assign bit_extender_5_out = {{12{1'b0}}, BCD_Lowest};  // Bit_Extender bit_extender_5
  Multiplexer #(.width(16), .enable("false")) multiplexer_2 (
    .in0(register_3_q), .in1(bit_extender_2_out), .out(multiplexer_2_out), .sel(wait_1_same_bit));
  Register #(.width(16), .Select("low")) register_1 (
    .D(multiplexer_1_out), .Q(register_1_q), .clk(register_7_q), .clr(or_1_out));  // open: en
  Multiplier #(.width(16)) multiplier_1 (.a(register_1_q), .b(16'h2710), .out(multiplier_1_out));  // open: cin, cout
  Priority_Encoder #(.select(4)) priority_encoder_1 (
    .in0(_0), .in1(in_4), .in2(in_5), .in3(in_6), .in4(in_7), .in5(in_8), .in6(in_9), .in7(in_10),
    .in8(in_11), .in9(in_12), .out(priority_encoder_1_out), .gs(priority_encoder_1_gs), .en_in(1'b1));  // open: in10, in11, in12, in13, in14, in15, en_out
  Register #(.width(16), .Select("low")) register_2 (
    .D(multiplexer_2_out), .Q(register_2_q), .clk(register_7_q), .clr(or_1_out));  // open: en
  Multiplexer #(.width(16), .enable("false")) multiplexer_3 (
    .in0(register_4_q), .in1(bit_extender_3_out), .out(multiplexer_3_out), .sel(wait_1_same_bit));
  Register #(.width(16), .Select("low")) register_3 (
    .D(multiplexer_3_out), .Q(register_3_q), .clk(register_7_q), .clr(or_1_out));  // open: en
  Multiplier #(.width(16)) multiplier_2 (.a(register_2_q), .b(16'h3e8), .out(multiplier_2_out));  // open: cin, cout
  Adder #(.width(16)) adder_1 (.a(multiplier_2_out), .b(multiplier_1_out), .out(adder_1_out));  // open: cin, cout
  D_Flip_Flop d_ff_1 (.clk(n), .D(d_ff_1_qn), .Q(Negate), .Qn(d_ff_1_qn));  // open: preset, reset
  Multiplexer #(.width(16), .enable("false")) multiplexer_4 (
    .in0(register_5_q), .in1(bit_extender_4_out), .out(multiplexer_4_out), .sel(wait_1_same_bit));
  Register #(.width(16), .Select("low")) register_4 (
    .D(multiplexer_4_out), .Q(register_4_q), .clk(register_7_q), .clr(or_1_out));  // open: en
  Multiplier #(.width(16)) multiplier_3 (.a(register_3_q), .b(16'h64), .out(multiplier_3_out));  // open: cin, cout
  Adder #(.width(16)) adder_2 (.a(multiplier_3_out), .b(adder_1_out), .out(adder_2_out));  // open: cin, cout
  Multiplexer #(.width(16), .enable("false")) multiplexer_5 (
    .in0({{12{1'b0}}, priority_encoder_1_out}), .in1(bit_extender_5_out), .out(multiplexer_5_out),
    .sel(wait_1_same_bit));
  Register #(.width(16), .Select("low")) register_5 (
    .D(multiplexer_5_out), .Q(register_5_q), .clk(register_7_q), .clr(or_1_out));  // open: en
  Multiplier #(.width(16)) multiplier_4 (.a(register_4_q), .b(16'ha), .out(multiplier_4_out));  // open: cin, cout
  or or_2 (or_2_out, n, or_1_out, priority_encoder_1_gs);
  or or_3 (or_3_out, priority_encoder_1_gs, wait_1_same_bit);
  Adder #(.width(16)) adder_3 (.a(multiplier_4_out), .b(adder_2_out), .out(adder_3_out));  // open: cin, cout
  Wait wait_1 (.Delay_1_for_4_ticks(Sync), .Clock(Clock_Line), .Same_bit(wait_1_same_bit));
  Register #(.width(1), .Select("low")) Wait_2 (
    .D(Change_Applied), .Q(Wait_2_q), .clk(Change_Applied), .clr(or_2_out));  // open: en
  and and_1 (and_1_out, ~or_2_out, Wait_2_q);  // AND_Gate
  Register #(.width(1), .Select("low")) register_6 (
    .Q(Changed), .clk(or_2_out), .clr(or_4_out), .preset(or_2_out));  // open: D, en, cs
  or or_4 (or_4_out, or_1_out, and_1_out);
  Adder #(.width(16)) adder_4 (.a(register_5_q), .b(adder_3_out), .out(adder_4_out));  // open: cin, cout
  Negator #(.width(16)) negator_1 (.in(adder_4_out), .out(negator_1_out));
  Register #(.width(1), .Select("low")) register_7 (.D(or_3_out), .Q(register_7_q), .clk(xor_1_out));  // open: en, clr
  xor xor_1 (xor_1_out, or_3_out, Clock_Line);
  Multiplexer #(.width(16), .enable("false")) multiplexer_6 (
    .in0(adder_4_out), .in1(negator_1_out), .out(Output), .sel(Negate));
endmodule

module Smart_Stack (
  input  [15:0] Extra_Data,
  input  When_1__load_from_ALU,
  input  Shift,
  input  No_push_mux,
  input  [15:0] Data_from_Enter,
  input  No_push_insert,
  input  [15:0] Data_from_ALU,
  input  [15:0] Remainer_from_ALU,
  input  Prepare_Rem,
  input  Put_Rem,
  input  AC,
  output [15:0] S1,
  output [15:0] S2,
  output [15:0] S3,
  output [15:0] S4,
  output [15:0] S5,
  output [15:0] S6
);

  wire and_1_out, multiplexer_2_out, not_1_out, or_1_out, or_2_out, or_3_out, undriven;
  wire [15:0] multiplexer_1_out, multiplexer_3_out, multiplexer_4_out, multiplexer_5_out, multiplexer_6_out,
       multiplexer_7_out, multiplexer_8_out, multiplexer_9_out, multiplexer_10_out, multiplexer_11_out,
       register_7_q;

  Multiplexer #(.width(16), .enable("false")) multiplexer_1 (
    .in0({16{1'b0}}), .in1(Remainer_from_ALU), .out(multiplexer_1_out), .sel(Prepare_Rem));
  Multiplexer #(.enable("false")) multiplexer_2 (
    .in0(When_1__load_from_ALU), .in1(1'b0), .out(multiplexer_2_out), .sel(When_1__load_from_ALU));
  Multiplexer #(.width(16), .enable("false")) multiplexer_3 (
    .in0(Data_from_Enter), .in1(Data_from_ALU), .out(multiplexer_3_out), .sel(When_1__load_from_ALU));
  and and_1 (and_1_out, Prepare_Rem, Put_Rem);
  Multiplexer #(.width(16), .enable("false")) multiplexer_4 (
    .in0(multiplexer_3_out), .in1(S2), .out(multiplexer_4_out), .sel(multiplexer_2_out));
  Multiplexer #(.width(16), .enable("false")) multiplexer_5 (
    .in0(S1), .in1(S3), .out(multiplexer_5_out), .sel(When_1__load_from_ALU));
  Multiplexer #(.width(16), .enable("false")) multiplexer_6 (
    .in0(S2), .in1(S4), .out(multiplexer_6_out), .sel(When_1__load_from_ALU));
  Multiplexer #(.width(16), .enable("false")) multiplexer_7 (
    .in0(S3), .in1(S5), .out(multiplexer_7_out), .sel(When_1__load_from_ALU));
  Multiplexer #(.width(16), .enable("false")) multiplexer_8 (
    .in0(S4), .in1(S6), .out(multiplexer_8_out), .sel(When_1__load_from_ALU));
  Multiplexer #(.width(16), .enable("false")) multiplexer_9 (
    .in0(S5), .in1(register_7_q), .out(multiplexer_9_out), .sel(When_1__load_from_ALU));
  or or_1 (or_1_out, When_1__load_from_ALU, Prepare_Rem);
  Multiplexer #(.width(16), .enable("false")) multiplexer_10 (
    .in0(S6), .in1(multiplexer_1_out), .out(multiplexer_10_out), .sel(or_1_out));
  Register #(.width(16), .Select("low")) register_1 (
    .D(multiplexer_11_out), .Q(S1), .clk(or_3_out), .clr(AC));  // open: en
  Multiplexer #(.width(16), .enable("false")) multiplexer_11 (
    .in0(Extra_Data), .in1(multiplexer_4_out), .out(multiplexer_11_out), .sel(not_1_out));
  Register #(.width(16), .Select("low")) register_2 (.D(multiplexer_5_out), .Q(S2), .clk(Shift), .clr(AC));  // open: en
  Register #(.width(16), .Select("low")) register_3 (.D(multiplexer_6_out), .Q(S3), .clk(Shift), .clr(AC));  // open: en
  Register #(.width(16), .Select("low")) register_4 (.D(multiplexer_7_out), .Q(S4), .clk(Shift), .clr(AC));  // open: en
  Register #(.width(16), .Select("low")) register_5 (.D(multiplexer_8_out), .Q(S5), .clk(Shift), .clr(AC));  // open: en
  Register #(.width(16), .Select("low")) register_6 (
    .D(multiplexer_9_out), .en(undriven), .Q(S6), .clk(Shift), .clr(AC));
  or or_2 (or_2_out, and_1_out, Shift);
  Register #(.width(16), .Select("low")) register_7 (
    .D(multiplexer_10_out), .Q(register_7_q), .clk(or_2_out), .clr(AC));  // open: en
  not not_1 (not_1_out, No_push_mux);
  or or_3 (or_3_out, No_push_insert, Shift);

  // Notes on the sheet:
  //   Remainer Special Stack
endmodule

module ALU (
  input  [11:0] Instruction,
  input  ALU_Called,
  input  Prepare_MUX,
  input  Start_Calc,
  input  Clock,
  input  [15:0] Op_1,
  input  [15:0] Op_2,
  output [15:0] SUM,
  output [15:0] SUB,
  output [15:0] MUL,
  output [15:0] DIV,
  output [15:0] DIV_Remainer,
  output [15:0] FACT,
  output [15:0] POW,
  output [15:0] out_15,
  output Fact_F,
  output Error_Flag,
  output Pow_Flag
);

  wire and_1_out, and_2_out, and_3_out, and_4_out, and_5_out, and_6_out, and_7_out, and_8_out, and_9_out,
       and_10_out, and_11_out, and_12_out, and_13_out, comparator_1_eq, comparator_2_eq, comparator_2_lt,
       comparator_3_eq, comparator_4_eq, comparator_5_lt, comparator_6_gt, comparator_7_eq, comparator_8_eq,
       comparator_9_eq, comparator_10_eq, comparator_11_eq, not_1_out, not_2_out, or_1_out, or_3_out,
       or_5_out;
  wire [15:0] counter_1_q, counter_2_q, div_general_1_q, div_general_1_r, multiplexer_3_out,
       multiplexer_4_out, multiplexer_6_out, multiplexer_7_out, multiplexer_9_out, multiplexer_10_out,
       multiplier_3_out, register_1_q, register_2_q, register_3_q, register_4_q, subtractor_2_out;

  Adder #(.width(16)) adder_1 (.a(Op_1), .b(Op_2), .out(SUM));  // open: cin, cout
  Subtractor #(.width(16)) subtractor_1 (.a(Op_2), .b(Op_1), .out(SUB));  // open: bin, bout
  Multiplier #(.width(16)) multiplier_1 (.a(Op_2), .b(Op_1), .out(MUL));  // open: cin, cout
  Div_General div_general_1 (.a(Op_2), .b(Op_1), .q(div_general_1_q), .r(div_general_1_r));
  Comparator #(.width(16)) comparator_1 (.a(Op_2), .b({16{1'b0}}), .eq(comparator_1_eq));  // open: gt, lt
  Comparator #(.width(16)) comparator_2 (
    .a(Op_1), .b({16{1'b0}}), .eq(comparator_2_eq), .lt(comparator_2_lt));  // open: gt
  and and_1 (and_1_out, ~comparator_11_eq, Prepare_MUX);  // AND_Gate
  or or_1 (or_1_out, comparator_1_eq, comparator_2_eq);
  Comparator #(.width(12)) comparator_3 (.a(Instruction), .b(12'h104), .eq(comparator_3_eq));  // open: gt, lt
  and and_2 (and_2_out, ALU_Called, ~and_1_out, ~Start_Calc);  // AND_Gate
  Multiplexer #(.width(16), .enable("false")) multiplexer_1 (
    .in0(div_general_1_q), .in1({16{1'b0}}), .out(DIV), .sel(or_1_out));
  and and_3 (and_3_out, comparator_2_eq, comparator_3_eq);
  Multiplexer #(.width(16), .enable("false")) multiplexer_2 (
    .in0(div_general_1_r), .in1({16{1'b0}}), .out(DIV_Remainer), .sel(or_1_out));
  and and_4 (and_4_out, comparator_2_lt, comparator_8_eq);
  or or_2 (Error_Flag, and_3_out, and_4_out, and_8_out, and_5_out);
  and and_5 (and_5_out, comparator_4_eq, comparator_5_lt);
  Comparator #(.width(12)) comparator_4 (.a(Instruction), .b(12'h105), .eq(comparator_4_eq));  // open: gt, lt
  Multiplexer #(.width(16), .enable("false")) multiplexer_3 (
    .in0(out_15), .in1(16'h1), .out(multiplexer_3_out), .sel(and_1_out));
  and and_6 (and_6_out, not_1_out, and_7_out);
  Multiplexer #(.width(16), .enable("false")) multiplexer_4 (
    .in0(counter_1_q), .in1(16'h1), .out(multiplexer_4_out), .sel(and_1_out));
  Comparator #(.width(16)) comparator_5 (.a(Op_1), .b({16{1'b0}}), .lt(comparator_5_lt));  // open: gt, eq
  and and_7 (and_7_out, Clock, or_3_out);
  or or_3 (or_3_out, Start_Calc, comparator_11_eq);
  Register #(.width(16), .Select("low")) register_1 (
    .D(multiplexer_3_out), .Q(register_1_q), .clk(and_6_out), .clr(and_2_out));  // open: en
  Counter #(.width(16), .max('hffff)) counter_1 (
    .load(and_1_out), .D(multiplexer_4_out), .count(not_1_out), .Q(counter_1_q), .clk(and_7_out),
    .clr(and_2_out));  // open: carry, preset, down
  Multiplexer #(.width(16), .enable("false")) multiplexer_5 (
    .in0(multiplexer_6_out), .in1({16{1'b0}}), .out(FACT), .sel(comparator_5_lt));
  Multiplexer #(.width(16), .enable("false")) multiplexer_6 (
    .in0(register_1_q), .in1(16'h1), .out(multiplexer_6_out), .sel(comparator_2_eq));
  and and_8 (and_8_out, comparator_8_eq, and_9_out);
  not not_1 (not_1_out, comparator_6_gt);
  Multiplier #(.width(16)) multiplier_2 (.a(register_1_q), .b(counter_1_q), .out(out_15));  // open: cin, cout
  Comparator #(.width(16)) comparator_6 (.a(counter_1_q), .b(Op_1), .gt(comparator_6_gt));  // open: eq, lt
  and and_9 (and_9_out, comparator_1_eq, comparator_2_eq);
  Comparator #(.width(12)) comparator_7 (.a(Instruction), .b(12'hc00), .eq(comparator_7_eq));  // open: gt, lt
  and and_10 (and_10_out, comparator_2_eq, comparator_7_eq);
  and and_11 (and_11_out, comparator_7_eq, comparator_6_gt);
  Register #(.width(16), .Select("low")) register_2 (.D(Op_1), .Q(register_2_q), .clk(Clock));  // open: en, clr
  Register #(.width(16), .Select("low")) register_3 (.D(Op_2), .Q(register_3_q), .clk(Clock));  // open: en, clr
  Comparator #(.width(12)) comparator_8 (.a(Instruction), .b(12'h106), .eq(comparator_8_eq));  // open: gt, lt
  or or_4 (Fact_F, and_10_out, and_11_out);
  Counter #(.width(16), .max('hffff)) counter_2 (
    .load(and_1_out), .D(register_2_q), .count(not_2_out), .Q(counter_2_q), .clk(and_7_out), .clr(and_2_out),
    .down(1'b1));  // open: carry, preset
  Register #(.width(16), .Select("low")) register_4 (
    .D(multiplexer_7_out), .en(not_2_out), .Q(register_4_q), .clk(and_7_out), .clr(and_2_out));
  Multiplexer #(.width(16), .enable("false")) multiplexer_7 (
    .in0(multiplier_3_out), .in1(register_3_q), .out(multiplexer_7_out), .sel(and_1_out));
  Multiplexer #(.width(16), .enable("false")) multiplexer_8 (
    .in0(multiplexer_9_out), .in1({16{1'b0}}), .out(POW), .sel(and_9_out));
  Multiplexer #(.width(16), .enable("false")) multiplexer_9 (
    .in0(multiplexer_10_out), .in1(16'h1), .out(multiplexer_9_out), .sel(comparator_2_eq));
  Multiplexer #(.width(16), .enable("false")) multiplexer_10 (
    .in0(register_4_q), .in1({16{1'b0}}), .out(multiplexer_10_out), .sel(comparator_2_lt));
  Subtractor #(.width(16)) subtractor_2 (.a(counter_2_q), .b(16'h1), .out(subtractor_2_out));  // open: bin, bout
  Multiplier #(.width(16)) multiplier_3 (
    .a(register_4_q), .b(register_3_q), .out(multiplier_3_out));  // open: cin, cout
  Comparator #(.width(16)) comparator_9 (.a(subtractor_2_out), .b({16{1'b0}}), .eq(comparator_9_eq));  // open: gt, lt
  Comparator #(.width(12)) comparator_10 (.a(Instruction), .b(12'hc11), .eq(comparator_10_eq));  // open: gt, lt
  Comparator #(.width(4)) comparator_11 (.a(Instruction[11:8]), .b(4'b1100), .eq(comparator_11_eq));  // open: gt, lt
  not not_2 (not_2_out, comparator_9_eq);
  or or_5 (or_5_out, comparator_2_lt, comparator_2_eq, and_9_out);
  and and_12 (and_12_out, or_5_out, comparator_10_eq);
  and and_13 (and_13_out, comparator_10_eq, comparator_9_eq);
  or or_6 (Pow_Flag, and_12_out, and_13_out);

  // Notes on the sheet:
  //   B
  //   A
  //   Factorial
  //   Exponent
  //   Base
  //   A / B
  //   Compare Operants to 0
  //   Dont Use Mux When Calculing
  //   Div Move Called
  //   Div by 0 Switch
  //   Fact Move Called
  //   Factorial Negative Error Switch
  //   Buffer
  //   Pow Move Called
  //   Trigger Flag ONLY when waiting for one
  //   Buffer
  //   Counter
  //   Power
  //   0^0 Switch Case
  //   x^0 Switch Case
  //   x^neg Switch Case
  //   Trigger Flag ONLY when waiting for one
endmodule

module Interrupt (
  input  Interrupt_Flag,
  input  Release_On_Instruction_Check,
  input  Clock_Line,
  output Effective_Release_Trigerred,
  output Skip_Interrupt_Instructions
);

  wire and_1_out, register_1_q, register_2_q, register_3_q;

  Register #(.width(1), .Select("low")) register_1 (
    .D(Interrupt_Flag), .en(Effective_Release_Trigerred), .Q(register_1_q), .clk(Interrupt_Flag),
    .clr(Release_On_Instruction_Check));
  Register #(.width(1), .Select("low")) register_2 (
    .D(Interrupt_Flag), .Q(register_2_q), .clk(Interrupt_Flag), .clr(and_1_out), .preset(register_1_q));  // open: en, cs
  and and_1 (and_1_out, ~register_1_q, Effective_Release_Trigerred);  // AND_Gate
  Register #(.width(1), .Select("low")) register_3 (
    .D(Release_On_Instruction_Check), .Q(register_3_q), .clk(Release_On_Instruction_Check),
    .clr(Effective_Release_Trigerred));  // open: en
  not not_1 (Skip_Interrupt_Instructions, register_2_q);
  Register #(.width(1), .Select("low")) register_4 (
    .D(register_3_q), .Q(Effective_Release_Trigerred), .clk(Clock_Line));  // open: en, clr
endmodule

module Wait (
  input  Delay_1_for_4_ticks,
  input  Clock,
  output Same_bit
);

  wire register_1_q, register_2_q, register_3_q, register_4_q;

  Register #(.width(1), .Select("low")) register_1 (
    .D(Delay_1_for_4_ticks), .Q(register_1_q), .clk(Delay_1_for_4_ticks), .clr(register_2_q));  // open: en
  Register #(.width(1), .Select("low")) register_2 (.D(register_1_q), .Q(register_2_q), .clk(Clock));  // open: en, clr
  Register #(.width(1), .Select("low")) register_3 (.D(register_4_q), .Q(register_3_q), .clk(Clock));  // open: en, clr
  Register #(.width(1), .Select("low")) register_4 (.D(register_2_q), .Q(register_4_q), .clk(Clock));  // open: en, clr
  Register #(.width(1), .Select("low")) register_5 (.D(register_3_q), .Q(Same_bit), .clk(Clock));  // open: en, clr
endmodule

module Error_System (
  input  Error,
  input  Clear,
  output E_symbol
);

  Register #(.width(1), .Select("low")) register_1 (.D(Error), .Q(E_symbol), .clk(Error), .clr(Clear));  // open: en
endmodule

module Div_General (
  input  [15:0] a,
  input  [15:0] b,
  output [15:0] q,
  output [15:0] r
);

  wire xor_1_out;
  wire [15:0] divider_1_out, divider_1_rem, multiplexer_1_out, multiplexer_2_out, negator_1_out,
       negator_2_out, negator_3_out, negator_4_out;

  Negator #(.width(16)) negator_1 (.in(a), .out(negator_1_out));
  Negator #(.width(16)) negator_2 (.in(b), .out(negator_2_out));
  Multiplexer #(.width(16), .enable("false")) multiplexer_1 (
    .in0(a), .in1(negator_1_out), .out(multiplexer_1_out), .sel(a[15]));
  Multiplexer #(.width(16), .enable("false")) multiplexer_2 (
    .in0(b), .in1(negator_2_out), .out(multiplexer_2_out), .sel(b[15]));
  Divider #(.width(16)) divider_1 (
    .a(multiplexer_1_out), .b(multiplexer_2_out), .out(divider_1_out), .rem(divider_1_rem));  // open: upper
  Negator #(.width(16)) negator_3 (.in(divider_1_out), .out(negator_3_out));
  xor xor_1 (xor_1_out, a[15], b[15]);
  Negator #(.width(16)) negator_4 (.in(divider_1_rem), .out(negator_4_out));
  Multiplexer #(.width(16), .enable("false")) multiplexer_3 (
    .in0(divider_1_out), .in1(negator_3_out), .out(q), .sel(xor_1_out));
  Multiplexer #(.width(16), .enable("false")) multiplexer_4 (
    .in0(divider_1_rem), .in1(negator_4_out), .out(r), .sel(a[15]));
endmodule
